// Logisim project SOBOL.circ as structural Verilog: 14 circuits, main circuit main
module main (
);

  wire clock_1_out, comparator_1_eq, comparator_1_gt, controlled_buffer_1_out, controlled_buffer_2_out,
       controlled_buffer_67_out, controlled_buffer_68_out, controlled_buffer_69_out,
       controlled_buffer_70_out, controlled_buffer_71_out, controlled_buffer_72_out, equals_1_res,
       equals_2_res, equals_3_res, equals_4_res, equals_5_res, equals_6_res, equals_7_res, equals_8_res,
       equals_9_res, equals_10_res, equals_11_res, equals_12_res, equals_13_res, equals_14_res,
       equals_15_res, equals_16_res, equals_17_res, equals_18_res, equals_19_res, equals_20_res,
       equals_21_res, equals_22_res, equals_23_res, equals_24_res, equals_25_res, equals_26_res,
       equals_27_res, equals_28_res, equals_29_res, equals_30_res, equals_31_res, equals_32_res,
       equals_33_res, equals_34_res, equals_35_res, equals_36_res, equals_37_res, equals_38_res,
       equals_39_res, equals_40_res, equals_41_res, equals_42_res, equals_43_res, equals_44_res,
       equals_45_res, equals_46_res, equals_47_res, equals_48_res, equals_49_res, equals_50_res,
       equals_51_res, equals_52_res, equals_53_res, equals_54_res, equals_55_res, equals_56_res,
       equals_57_res, equals_58_res, equals_59_res, equals_60_res, equals_61_res, equals_62_res,
       equals_63_res, equals_64_res, equals_65_res, equals_66_res, equals_67_res, equals_68_res,
       equals_69_res, equals_70_res, equals_71_res, equals_72_res, equals_73_res, equals_74_res,
       equals_75_res, equals_76_res, equals_77_res, equals_78_res, equals_79_res, equals_80_res,
       equals_81_res, equals_82_res, equals_83_res, equals_84_res, equals_85_res, equals_86_res,
       equals_87_res, equals_88_res, equals_89_res, equals_90_res, equals_91_res, equals_92_res,
       equals_93_res, equals_94_res, equals_95_res, equals_96_res, equals_97_res, equals_98_res,
       equals_99_res, Main_Programm_p1, nctotf_1_res, nctotf_2_res, nctotf_3_res, nctotf_4_res, nctotf_5_res,
       nctotf_6_res, nctotf_7_res, nctotf_8_res, nctotf_9_res, nctotf_10_res, nctotf_11_res, nctotf_12_res,
       nctotf_13_res, nctotf_14_res, nctotf_15_res, nctotf_16_res, nctotf_17_res, nctotf_18_res,
       nctotf_19_res, nctotf_20_res, nctotf_21_res, nctotf_22_res, nctotf_23_res, nctotf_24_res,
       nctotf_25_res, nctotf_26_res, nctotf_27_res, nctotf_28_res, nctotf_29_res, nctotf_30_res,
       nctotf_31_res, nctotf_32_res, nctotf_33_res, nctotf_34_res, nctotf_35_res, nctotf_36_res,
       nctotf_37_res, nctotf_38_res, nctotf_39_res, nctotf_40_res, nctotf_41_res, nctotf_42_res,
       nctotf_43_res, nctotf_44_res, nctotf_45_res, nctotf_46_res, nctotf_47_res, nctotf_48_res,
       nctotf_49_res, nctotf_50_res, nctotf_51_res, nctotf_52_res, nctotf_53_res, nctotf_54_res,
       nctotf_55_res, nctotf_56_res, nctotf_57_res, nctotf_58_res, nctotf_59_res, nctotf_60_res,
       nctotf_61_res, nctotf_62_res, nctotf_63_res, nctotf_64_res, nctotf_65_res, nctotf_66_res,
       nctotf_67_res, nctotf_68_res, nctotf_69_res, nctotf_70_res, nctotf_71_res, nctotf_72_res,
       nctotf_73_res, nctotf_74_res, nctotf_75_res, nctotf_76_res, nctotf_77_res, nctotf_78_res,
       nctotf_79_res, nctotf_80_res, nctotf_81_res, nctotf_82_res, nctotf_83_res, nctotf_84_res,
       nctotf_85_res, nctotf_86_res, nctotf_87_res, nctotf_88_res, nctotf_89_res, nctotf_90_res,
       nctotf_91_res, nctotf_92_res, nctotf_93_res, nctotf_94_res, nctotf_95_res, nctotf_96_res,
       nctotf_97_res, nctotf_98_res, nctotf_99_res, nctotf_100_res, not_1_out, or_1_out, or_2_out, or_3_out,
       or_4_out, or_5_out, por_1_out, Prepare_Register_q, register_33_q, register_34_q, register_35_q,
       register_36_q, register_37_q, register_38_q, register_39_q, register_40_q, RESET_out, smallor_1_out_3,
       smallor_2_out_3, smallor_3_out_3, smallor_4_out_3, smallor_5_out_3, smallor_6_out_3, smallor_7_out_3,
       smallor_8_out_3, summod_1_carryout, summod_1_halfcarryout, summod_1_isazero, summod_1_nev,
       summod_1_sign, tftonc_1_out_2, tftonc_2_out_2, tftonc_3_out_2, tftonc_4_out_2, tftonc_5_out_2,
       tftonc_6_out_2, undriven, undriven_2, undriven_3, undriven_4, undriven_5, undriven_6, undriven_7,
       undriven_8, undriven_9, undriven_10, undriven_11, undriven_12, undriven_13, undriven_14, undriven_15,
       undriven_16;
  wire [7:0] buscontrol_1_out_6, buscontrol_1_out_8, buscontrol_2_out_7, buscontrol_2_out_8,
       buscontrol_3_out_6, buscontrol_3_out_7, buscontrol_3_out_8, buscontrol_3_out_9,
       controlled_buffer_3_out, controlled_buffer_4_out, controlled_buffer_73_out, controlled_buffer_74_out,
       increment_1_out_2, increment_2_out_2, increment_3_out_2, increment_4_out_2, increment_5_out_2,
       increment_6_out_2, increment_7_out_2, increment_8_out_2, increment_9_out_2, increment_10_out_2,
       increment_11_out_2, increment_12_out_2, increment_13_out_2, increment_14_out_2, increment_15_out_2,
       increment_16_out_2, increment_17_out_2, increment_18_out_2, increment_19_out_2, increment_20_out_2,
       increment_21_out_2, increment_22_out_2, increment_23_out_2, increment_24_out_2, increment_25_out_2,
       increment_26_out_2, increment_27_out_2, increment_28_out_2, increment_29_out_2, increment_30_out_2,
       increment_31_out_2, Main_Counter_q, Main_Programm_p3, Main_Programm_p4, Main_Programm_p5,
       Main_Programm_p6, multiplexer_1_out, multiplier_1_out, register_1_q, register_2_q, register_3_q,
       register_4_q, register_5_q, register_6_q, register_7_q, register_8_q, register_9_q, register_10_q,
       register_11_q, register_12_q, register_13_q, register_14_q, register_15_q, register_16_q,
       register_17_q, register_18_q, register_19_q, register_20_q, register_21_q, register_22_q,
       register_23_q, register_24_q, register_25_q, register_26_q, register_27_q, register_28_q,
       register_29_q, register_30_q, register_31_q, register_32_q, summod_1_result, Watchdog_Timer_Counter_q,
       Watchdog_Timer_sw8;

  Clock clock_1 (.out(clock_1_out));
  Counter Main_Counter (
    .clr(or_2_out), .load(nctotf_3_res), .up(undriven_3), .count(not_1_out), .clk(controlled_buffer_1_out),
    .D(buscontrol_2_out_7), .Q(Main_Counter_q));  // open: carry
  // NoConnect on undriven_3
  not not_1 (not_1_out, nctotf_3_res);
  Register #(.trigger("falling"), .width(1)) Prepare_Register (
    .D(1'b1), .en(1'b1), .clk(or_3_out), .Q(Prepare_Register_q), .clr(or_2_out));
  Counter #(.ongoal("stay")) Watchdog_Timer_Counter (
    .clr(undriven), .count(or_1_out), .clk(or_3_out), .Q(Watchdog_Timer_Counter_q));  // open: load, up, D, carry
  or or_1 (or_1_out, or_2_out, nctotf_1_res);
  NCtoTF nctotf_1 (.A(undriven_2), .res(nctotf_1_res));
  or or_2 (or_2_out, RESET_out, nctotf_2_res, por_1_out);
  Button RESET (.out(RESET_out));
  NCtoTF nctotf_2 (.A(controlled_buffer_2_out), .res(nctotf_2_res));
  POR #(.PorHighDuration(1)) por_1 (.out(por_1_out));
  DipSwitch Watchdog_Timer (
    .sw1(Watchdog_Timer_sw8[7]), .sw2(Watchdog_Timer_sw8[6]), .sw3(Watchdog_Timer_sw8[5]),
    .sw4(Watchdog_Timer_sw8[4]), .sw5(Watchdog_Timer_sw8[3]), .sw6(Watchdog_Timer_sw8[2]),
    .sw7(Watchdog_Timer_sw8[1]), .sw8(Watchdog_Timer_sw8[0]));
  NCtoTF nctotf_3 (.A(Main_Programm_p1), .res(nctotf_3_res));
  assign controlled_buffer_1_out = Prepare_Register_q ? or_3_out : 1'bz;  // Controlled_Buffer controlled_buffer_1
  or or_3 (or_3_out, por_1_out, clock_1_out);
  // Probe on Watchdog_Timer_Counter_q
  // Probe on Watchdog_Timer_sw8
  Multiplier multiplier_1 (.a(8'h4), .b(Main_Counter_q), .out(multiplier_1_out));  // open: cin, cout
  NCtoTF nctotf_4 (.A(register_40_q), .res(nctotf_4_res));
  Comparator #(.mode("unsigned")) comparator_1 (
    .a(Watchdog_Timer_Counter_q), .b(Watchdog_Timer_sw8), .gt(comparator_1_gt), .eq(comparator_1_eq));  // open: lt
  // ROM #(.addrWidth(10), .line("quad")) Main_Programm: pin names not known; wires that end beside it: Main_Programm_p1, {2'b00, multiplier_1_out}, Main_Programm_p3, Main_Programm_p4, Main_Programm_p5, Main_Programm_p6
  // Probe on buscontrol_2_out_8
  // Probe on buscontrol_2_out_7
  increment increment_1 (.in_1({8{1'b0}}), .out_2(increment_1_out_2));
  increment increment_2 (.in_1(increment_1_out_2), .out_2(increment_2_out_2));
  increment increment_3 (.in_1(increment_2_out_2), .out_2(increment_3_out_2));
  assign controlled_buffer_2_out = nctotf_4_res ? or_4_out : 1'bz;  // Controlled_Buffer controlled_buffer_2
  or or_4 (or_4_out, comparator_1_gt, comparator_1_eq);
  increment increment_4 (.in_1(increment_3_out_2), .out_2(increment_4_out_2));
  increment increment_5 (.in_1(increment_4_out_2), .out_2(increment_5_out_2));
  increment increment_6 (.in_1(increment_5_out_2), .out_2(increment_6_out_2));
  increment increment_7 (.in_1(increment_6_out_2), .out_2(increment_7_out_2));
  increment increment_8 (.in_1(increment_7_out_2), .out_2(increment_8_out_2));
  increment increment_9 (.in_1(increment_8_out_2), .out_2(increment_9_out_2));
  increment increment_10 (.in_1(increment_9_out_2), .out_2(increment_10_out_2));
  increment increment_11 (.in_1(increment_10_out_2), .out_2(increment_11_out_2));
  increment increment_12 (.in_1(increment_11_out_2), .out_2(increment_12_out_2));
  increment increment_13 (.in_1(increment_12_out_2), .out_2(increment_13_out_2));
  increment increment_14 (.in_1(increment_13_out_2), .out_2(increment_14_out_2));
  increment increment_15 (.in_1(increment_14_out_2), .out_2(increment_15_out_2));
  increment increment_16 (.in_1(increment_15_out_2), .out_2(increment_16_out_2));
  increment increment_17 (.in_1(increment_16_out_2), .out_2(increment_17_out_2));
  increment increment_18 (.in_1(increment_17_out_2), .out_2(increment_18_out_2));
  increment increment_19 (.in_1(increment_18_out_2), .out_2(increment_19_out_2));
  increment increment_20 (.in_1(increment_19_out_2), .out_2(increment_20_out_2));
  increment increment_21 (.in_1(increment_20_out_2), .out_2(increment_21_out_2));
  increment increment_22 (.in_1(increment_21_out_2), .out_2(increment_22_out_2));
  increment increment_23 (.in_1(increment_22_out_2), .out_2(increment_23_out_2));
  increment increment_24 (.in_1(increment_23_out_2), .out_2(increment_24_out_2));
  increment increment_25 (.in_1(increment_24_out_2), .out_2(increment_25_out_2));
  increment increment_26 (.in_1(increment_25_out_2), .out_2(increment_26_out_2));
  increment increment_27 (.in_1(increment_26_out_2), .out_2(increment_27_out_2));
  increment increment_28 (.in_1(increment_27_out_2), .out_2(increment_28_out_2));
  increment increment_29 (.in_1(increment_28_out_2), .out_2(increment_29_out_2));
  increment increment_30 (.in_1(increment_29_out_2), .out_2(increment_30_out_2));
  increment increment_31 (.in_1(increment_30_out_2), .out_2(increment_31_out_2));
  Register register_1 (.D(buscontrol_2_out_7), .en(nctotf_5_res), .clk(or_3_out), .Q(register_1_q), .clr(or_2_out));
  Equals equals_1 (.A(buscontrol_2_out_8), .B({8{1'b0}}), .res(equals_1_res));
  NCtoTF nctotf_5 (.A(equals_1_res), .res(nctotf_5_res));
  Register register_2 (.D(buscontrol_2_out_7), .en(nctotf_6_res), .clk(or_3_out), .Q(register_2_q), .clr(or_2_out));
  Equals equals_2 (.A(buscontrol_2_out_8), .B(increment_1_out_2), .res(equals_2_res));
  NCtoTF nctotf_6 (.A(equals_2_res), .res(nctotf_6_res));
  Register register_3 (.D(buscontrol_2_out_7), .en(nctotf_7_res), .clk(or_3_out), .Q(register_3_q), .clr(or_2_out));
  Equals equals_3 (.A(buscontrol_2_out_8), .B(increment_2_out_2), .res(equals_3_res));
  NCtoTF nctotf_7 (.A(equals_3_res), .res(nctotf_7_res));
  Register register_4 (.D(buscontrol_2_out_7), .en(nctotf_8_res), .clk(or_3_out), .Q(register_4_q), .clr(or_2_out));
  Equals equals_4 (.A(buscontrol_2_out_8), .B(increment_3_out_2), .res(equals_4_res));
  NCtoTF nctotf_8 (.A(equals_4_res), .res(nctotf_8_res));
  Register register_5 (.D(buscontrol_2_out_7), .en(nctotf_9_res), .clk(or_3_out), .Q(register_5_q), .clr(or_2_out));
  Equals equals_5 (.A(buscontrol_2_out_8), .B(increment_4_out_2), .res(equals_5_res));
  NCtoTF nctotf_9 (.A(equals_5_res), .res(nctotf_9_res));
  Register register_6 (.D(buscontrol_2_out_7), .en(nctotf_10_res), .clk(or_3_out), .Q(register_6_q), .clr(or_2_out));
  Equals equals_6 (.A(buscontrol_2_out_8), .B(increment_5_out_2), .res(equals_6_res));
  NCtoTF nctotf_10 (.A(equals_6_res), .res(nctotf_10_res));
  Register register_7 (.D(buscontrol_2_out_7), .en(nctotf_11_res), .clk(or_3_out), .Q(register_7_q), .clr(or_2_out));
  Equals equals_7 (.A(buscontrol_2_out_8), .B(increment_6_out_2), .res(equals_7_res));
  NCtoTF nctotf_11 (.A(equals_7_res), .res(nctotf_11_res));
  Register register_8 (.D(buscontrol_2_out_7), .en(nctotf_12_res), .clk(or_3_out), .Q(register_8_q), .clr(or_2_out));
  Equals equals_8 (.A(buscontrol_2_out_8), .B(increment_7_out_2), .res(equals_8_res));
  NCtoTF nctotf_12 (.A(equals_8_res), .res(nctotf_12_res));
  Register register_9 (.D(buscontrol_2_out_7), .en(nctotf_13_res), .clk(or_3_out), .Q(register_9_q), .clr(or_2_out));
  Equals equals_9 (.A(buscontrol_2_out_8), .B(increment_8_out_2), .res(equals_9_res));
  NCtoTF nctotf_13 (.A(equals_9_res), .res(nctotf_13_res));
  Register register_10 (.D(buscontrol_2_out_7), .en(nctotf_14_res), .clk(or_3_out), .Q(register_10_q), .clr(or_2_out));
  Equals equals_10 (.A(buscontrol_2_out_8), .B(increment_9_out_2), .res(equals_10_res));
  NCtoTF nctotf_14 (.A(equals_10_res), .res(nctotf_14_res));
  Register register_11 (.D(buscontrol_2_out_7), .en(nctotf_15_res), .clk(or_3_out), .Q(register_11_q), .clr(or_2_out));
  Equals equals_11 (.A(buscontrol_2_out_8), .B(increment_10_out_2), .res(equals_11_res));
  NCtoTF nctotf_15 (.A(equals_11_res), .res(nctotf_15_res));
  Register register_12 (.D(buscontrol_2_out_7), .en(nctotf_16_res), .clk(or_3_out), .Q(register_12_q), .clr(or_2_out));
  Equals equals_12 (.A(buscontrol_2_out_8), .B(increment_11_out_2), .res(equals_12_res));
  NCtoTF nctotf_16 (.A(equals_12_res), .res(nctotf_16_res));
  Register register_13 (.D(buscontrol_2_out_7), .en(nctotf_17_res), .clk(or_3_out), .Q(register_13_q), .clr(or_2_out));
  Equals equals_13 (.A(buscontrol_2_out_8), .B(increment_12_out_2), .res(equals_13_res));
  NCtoTF nctotf_17 (.A(equals_13_res), .res(nctotf_17_res));
  Register register_14 (.D(buscontrol_2_out_7), .en(nctotf_18_res), .clk(or_3_out), .Q(register_14_q), .clr(or_2_out));
  Equals equals_14 (.A(buscontrol_2_out_8), .B(increment_13_out_2), .res(equals_14_res));
  NCtoTF nctotf_18 (.A(equals_14_res), .res(nctotf_18_res));
  Register register_15 (.D(buscontrol_2_out_7), .en(nctotf_19_res), .clk(or_3_out), .Q(register_15_q), .clr(or_2_out));
  Equals equals_15 (.A(buscontrol_2_out_8), .B(increment_14_out_2), .res(equals_15_res));
  NCtoTF nctotf_19 (.A(equals_15_res), .res(nctotf_19_res));
  Register register_16 (.D(buscontrol_2_out_7), .en(nctotf_20_res), .clk(or_3_out), .Q(register_16_q), .clr(or_2_out));
  Equals equals_16 (.A(buscontrol_2_out_8), .B(increment_15_out_2), .res(equals_16_res));
  NCtoTF nctotf_20 (.A(equals_16_res), .res(nctotf_20_res));
  Register register_17 (.D(buscontrol_2_out_7), .en(nctotf_21_res), .clk(or_3_out), .Q(register_17_q), .clr(or_2_out));
  Equals equals_17 (.A(buscontrol_2_out_8), .B(increment_16_out_2), .res(equals_17_res));
  NCtoTF nctotf_21 (.A(equals_17_res), .res(nctotf_21_res));
  Register register_18 (.D(buscontrol_2_out_7), .en(nctotf_22_res), .clk(or_3_out), .Q(register_18_q), .clr(or_2_out));
  Equals equals_18 (.A(buscontrol_2_out_8), .B(increment_17_out_2), .res(equals_18_res));
  NCtoTF nctotf_22 (.A(equals_18_res), .res(nctotf_22_res));
  Register register_19 (.D(buscontrol_2_out_7), .en(nctotf_23_res), .clk(or_3_out), .Q(register_19_q), .clr(or_2_out));
  Equals equals_19 (.A(buscontrol_2_out_8), .B(increment_18_out_2), .res(equals_19_res));
  NCtoTF nctotf_23 (.A(equals_19_res), .res(nctotf_23_res));
  Register register_20 (.D(buscontrol_2_out_7), .en(nctotf_24_res), .clk(or_3_out), .Q(register_20_q), .clr(or_2_out));
  Equals equals_20 (.A(buscontrol_2_out_8), .B(increment_19_out_2), .res(equals_20_res));
  NCtoTF nctotf_24 (.A(equals_20_res), .res(nctotf_24_res));
  Register register_21 (.D(buscontrol_2_out_7), .en(nctotf_25_res), .clk(or_3_out), .Q(register_21_q), .clr(or_2_out));
  Equals equals_21 (.A(buscontrol_2_out_8), .B(increment_20_out_2), .res(equals_21_res));
  NCtoTF nctotf_25 (.A(equals_21_res), .res(nctotf_25_res));
  Register register_22 (.D(buscontrol_2_out_7), .en(nctotf_26_res), .clk(or_3_out), .Q(register_22_q), .clr(or_2_out));
  Equals equals_22 (.A(buscontrol_2_out_8), .B(increment_21_out_2), .res(equals_22_res));
  NCtoTF nctotf_26 (.A(equals_22_res), .res(nctotf_26_res));
  Register register_23 (.D(buscontrol_2_out_7), .en(nctotf_27_res), .clk(or_3_out), .Q(register_23_q), .clr(or_2_out));
  Equals equals_23 (.A(buscontrol_2_out_8), .B(increment_22_out_2), .res(equals_23_res));
  NCtoTF nctotf_27 (.A(equals_23_res), .res(nctotf_27_res));
  Register register_24 (.D(buscontrol_2_out_7), .en(nctotf_28_res), .clk(or_3_out), .Q(register_24_q), .clr(or_2_out));
  Equals equals_24 (.A(buscontrol_2_out_8), .B(increment_23_out_2), .res(equals_24_res));
  NCtoTF nctotf_28 (.A(equals_24_res), .res(nctotf_28_res));
  Register register_25 (.D(buscontrol_2_out_7), .en(nctotf_29_res), .clk(or_3_out), .Q(register_25_q), .clr(or_2_out));
  Equals equals_25 (.A(buscontrol_2_out_8), .B(increment_24_out_2), .res(equals_25_res));
  NCtoTF nctotf_29 (.A(equals_25_res), .res(nctotf_29_res));
  Register register_26 (.D(buscontrol_2_out_7), .en(nctotf_30_res), .clk(or_3_out), .Q(register_26_q), .clr(or_2_out));
  Equals equals_26 (.A(buscontrol_2_out_8), .B(increment_25_out_2), .res(equals_26_res));
  NCtoTF nctotf_30 (.A(equals_26_res), .res(nctotf_30_res));
  Register register_27 (.D(buscontrol_2_out_7), .en(nctotf_31_res), .clk(or_3_out), .Q(register_27_q), .clr(or_2_out));
  Equals equals_27 (.A(buscontrol_2_out_8), .B(increment_26_out_2), .res(equals_27_res));
  NCtoTF nctotf_31 (.A(equals_27_res), .res(nctotf_31_res));
  Register register_28 (.D(buscontrol_2_out_7), .en(nctotf_32_res), .clk(or_3_out), .Q(register_28_q), .clr(or_2_out));
  Equals equals_28 (.A(buscontrol_2_out_8), .B(increment_27_out_2), .res(equals_28_res));
  NCtoTF nctotf_32 (.A(equals_28_res), .res(nctotf_32_res));
  Register register_29 (.D(buscontrol_2_out_7), .en(nctotf_33_res), .clk(or_3_out), .Q(register_29_q), .clr(or_2_out));
  Equals equals_29 (.A(buscontrol_2_out_8), .B(increment_28_out_2), .res(equals_29_res));
  NCtoTF nctotf_33 (.A(equals_29_res), .res(nctotf_33_res));
  Register register_30 (.D(buscontrol_2_out_7), .en(nctotf_34_res), .clk(or_3_out), .Q(register_30_q), .clr(or_2_out));
  Equals equals_30 (.A(buscontrol_2_out_8), .B(increment_29_out_2), .res(equals_30_res));
  NCtoTF nctotf_34 (.A(equals_30_res), .res(nctotf_34_res));
  Register register_31 (.D(buscontrol_2_out_7), .en(nctotf_35_res), .clk(or_3_out), .Q(register_31_q), .clr(or_2_out));
  Equals equals_31 (.A(buscontrol_2_out_8), .B(increment_30_out_2), .res(equals_31_res));
  NCtoTF nctotf_35 (.A(equals_31_res), .res(nctotf_35_res));
  Register register_32 (.D(buscontrol_2_out_7), .en(nctotf_36_res), .clk(or_3_out), .Q(register_32_q), .clr(or_2_out));
  Equals equals_32 (.A(buscontrol_2_out_8), .B(increment_31_out_2), .res(equals_32_res));
  NCtoTF nctotf_36 (.A(equals_32_res), .res(nctotf_36_res));
  Equals equals_33 (.A(buscontrol_1_out_8), .B({8{1'b0}}), .res(equals_33_res));
  NCtoTF nctotf_37 (.A(equals_33_res), .res(nctotf_37_res));
  assign controlled_buffer_3_out = nctotf_37_res ? register_1_q : 8'bz;  // Controlled_Buffer controlled_buffer_3
  Equals equals_34 (.A(buscontrol_1_out_6), .B({8{1'b0}}), .res(equals_34_res));
  NCtoTF nctotf_38 (.A(equals_34_res), .res(nctotf_38_res));
  assign controlled_buffer_4_out = nctotf_38_res ? register_1_q : 8'bz;  // Controlled_Buffer controlled_buffer_4
  Equals equals_35 (.A(buscontrol_1_out_8), .B(increment_1_out_2), .res(equals_35_res));
  NCtoTF nctotf_39 (.A(equals_35_res), .res(nctotf_39_res));
  assign controlled_buffer_3_out = nctotf_39_res ? register_2_q : 8'bz;  // Controlled_Buffer controlled_buffer_5
  Equals equals_36 (.A(buscontrol_1_out_6), .B(increment_1_out_2), .res(equals_36_res));
  NCtoTF nctotf_40 (.A(equals_36_res), .res(nctotf_40_res));
  assign controlled_buffer_4_out = nctotf_40_res ? register_2_q : 8'bz;  // Controlled_Buffer controlled_buffer_6
  Equals equals_37 (.A(buscontrol_1_out_8), .B(increment_2_out_2), .res(equals_37_res));
  NCtoTF nctotf_41 (.A(equals_37_res), .res(nctotf_41_res));
  assign controlled_buffer_3_out = nctotf_41_res ? register_3_q : 8'bz;  // Controlled_Buffer controlled_buffer_7
  Equals equals_38 (.A(buscontrol_1_out_6), .B(increment_2_out_2), .res(equals_38_res));
  NCtoTF nctotf_42 (.A(equals_38_res), .res(nctotf_42_res));
  assign controlled_buffer_4_out = nctotf_42_res ? register_3_q : 8'bz;  // Controlled_Buffer controlled_buffer_8
  Equals equals_39 (.A(buscontrol_1_out_8), .B(increment_3_out_2), .res(equals_39_res));
  NCtoTF nctotf_43 (.A(equals_39_res), .res(nctotf_43_res));
  assign controlled_buffer_3_out = nctotf_43_res ? register_4_q : 8'bz;  // Controlled_Buffer controlled_buffer_9
  Equals equals_40 (.A(buscontrol_1_out_6), .B(increment_3_out_2), .res(equals_40_res));
  NCtoTF nctotf_44 (.A(equals_40_res), .res(nctotf_44_res));
  assign controlled_buffer_4_out = nctotf_44_res ? register_4_q : 8'bz;  // Controlled_Buffer controlled_buffer_10
  Equals equals_41 (.A(buscontrol_1_out_8), .B(increment_4_out_2), .res(equals_41_res));
  NCtoTF nctotf_45 (.A(equals_41_res), .res(nctotf_45_res));
  assign controlled_buffer_3_out = nctotf_45_res ? register_5_q : 8'bz;  // Controlled_Buffer controlled_buffer_11
  Equals equals_42 (.A(buscontrol_1_out_6), .B(increment_4_out_2), .res(equals_42_res));
  NCtoTF nctotf_46 (.A(equals_42_res), .res(nctotf_46_res));
  assign controlled_buffer_4_out = nctotf_46_res ? register_5_q : 8'bz;  // Controlled_Buffer controlled_buffer_12
  Equals equals_43 (.A(buscontrol_1_out_8), .B(increment_5_out_2), .res(equals_43_res));
  NCtoTF nctotf_47 (.A(equals_43_res), .res(nctotf_47_res));
  assign controlled_buffer_3_out = nctotf_47_res ? register_6_q : 8'bz;  // Controlled_Buffer controlled_buffer_13
  Equals equals_44 (.A(buscontrol_1_out_6), .B(increment_5_out_2), .res(equals_44_res));
  NCtoTF nctotf_48 (.A(equals_44_res), .res(nctotf_48_res));
  assign controlled_buffer_4_out = nctotf_48_res ? register_6_q : 8'bz;  // Controlled_Buffer controlled_buffer_14
  Equals equals_45 (.A(buscontrol_1_out_8), .B(increment_6_out_2), .res(equals_45_res));
  NCtoTF nctotf_49 (.A(equals_45_res), .res(nctotf_49_res));
  assign controlled_buffer_3_out = nctotf_49_res ? register_7_q : 8'bz;  // Controlled_Buffer controlled_buffer_15
  Equals equals_46 (.A(buscontrol_1_out_6), .B(increment_6_out_2), .res(equals_46_res));
  NCtoTF nctotf_50 (.A(equals_46_res), .res(nctotf_50_res));
  assign controlled_buffer_4_out = nctotf_50_res ? register_7_q : 8'bz;  // Controlled_Buffer controlled_buffer_16
  Equals equals_47 (.A(buscontrol_1_out_8), .B(increment_7_out_2), .res(equals_47_res));
  NCtoTF nctotf_51 (.A(equals_47_res), .res(nctotf_51_res));
  assign controlled_buffer_3_out = nctotf_51_res ? register_8_q : 8'bz;  // Controlled_Buffer controlled_buffer_17
  Equals equals_48 (.A(buscontrol_1_out_6), .B(increment_7_out_2), .res(equals_48_res));
  NCtoTF nctotf_52 (.A(equals_48_res), .res(nctotf_52_res));
  assign controlled_buffer_4_out = nctotf_52_res ? register_8_q : 8'bz;  // Controlled_Buffer controlled_buffer_18
  Equals equals_49 (.A(buscontrol_1_out_8), .B(increment_8_out_2), .res(equals_49_res));
  NCtoTF nctotf_53 (.A(equals_49_res), .res(nctotf_53_res));
  assign controlled_buffer_3_out = nctotf_53_res ? register_9_q : 8'bz;  // Controlled_Buffer controlled_buffer_19
  Equals equals_50 (.A(buscontrol_1_out_6), .B(increment_8_out_2), .res(equals_50_res));
  NCtoTF nctotf_54 (.A(equals_50_res), .res(nctotf_54_res));
  assign controlled_buffer_4_out = nctotf_54_res ? register_9_q : 8'bz;  // Controlled_Buffer controlled_buffer_20
  Equals equals_51 (.A(buscontrol_1_out_8), .B(increment_9_out_2), .res(equals_51_res));
  NCtoTF nctotf_55 (.A(equals_51_res), .res(nctotf_55_res));
  assign controlled_buffer_3_out = nctotf_55_res ? register_10_q : 8'bz;  // Controlled_Buffer controlled_buffer_21
  Equals equals_52 (.A(buscontrol_1_out_6), .B(increment_9_out_2), .res(equals_52_res));
  NCtoTF nctotf_56 (.A(equals_52_res), .res(nctotf_56_res));
  assign controlled_buffer_4_out = nctotf_56_res ? register_10_q : 8'bz;  // Controlled_Buffer controlled_buffer_22
  Equals equals_53 (.A(buscontrol_1_out_8), .B(increment_10_out_2), .res(equals_53_res));
  NCtoTF nctotf_57 (.A(equals_53_res), .res(nctotf_57_res));
  assign controlled_buffer_3_out = nctotf_57_res ? register_11_q : 8'bz;  // Controlled_Buffer controlled_buffer_23
  Equals equals_54 (.A(buscontrol_1_out_6), .B(increment_10_out_2), .res(equals_54_res));
  NCtoTF nctotf_58 (.A(equals_54_res), .res(nctotf_58_res));
  assign controlled_buffer_4_out = nctotf_58_res ? register_11_q : 8'bz;  // Controlled_Buffer controlled_buffer_24
  Equals equals_55 (.A(buscontrol_1_out_8), .B(increment_11_out_2), .res(equals_55_res));
  NCtoTF nctotf_59 (.A(equals_55_res), .res(nctotf_59_res));
  assign controlled_buffer_3_out = nctotf_59_res ? register_12_q : 8'bz;  // Controlled_Buffer controlled_buffer_25
  Equals equals_56 (.A(buscontrol_1_out_6), .B(increment_11_out_2), .res(equals_56_res));
  NCtoTF nctotf_60 (.A(equals_56_res), .res(nctotf_60_res));
  assign controlled_buffer_4_out = nctotf_60_res ? register_12_q : 8'bz;  // Controlled_Buffer controlled_buffer_26
  Equals equals_57 (.A(buscontrol_1_out_8), .B(increment_12_out_2), .res(equals_57_res));
  NCtoTF nctotf_61 (.A(equals_57_res), .res(nctotf_61_res));
  assign controlled_buffer_3_out = nctotf_61_res ? register_13_q : 8'bz;  // Controlled_Buffer controlled_buffer_27
  Equals equals_58 (.A(buscontrol_1_out_6), .B(increment_12_out_2), .res(equals_58_res));
  NCtoTF nctotf_62 (.A(equals_58_res), .res(nctotf_62_res));
  assign controlled_buffer_4_out = nctotf_62_res ? register_13_q : 8'bz;  // Controlled_Buffer controlled_buffer_28
  Equals equals_59 (.A(buscontrol_1_out_8), .B(increment_13_out_2), .res(equals_59_res));
  NCtoTF nctotf_63 (.A(equals_59_res), .res(nctotf_63_res));
  assign controlled_buffer_3_out = nctotf_63_res ? register_14_q : 8'bz;  // Controlled_Buffer controlled_buffer_29
  Equals equals_60 (.A(buscontrol_1_out_6), .B(increment_13_out_2), .res(equals_60_res));
  NCtoTF nctotf_64 (.A(equals_60_res), .res(nctotf_64_res));
  assign controlled_buffer_4_out = nctotf_64_res ? register_14_q : 8'bz;  // Controlled_Buffer controlled_buffer_30
  Equals equals_61 (.A(buscontrol_1_out_8), .B(increment_14_out_2), .res(equals_61_res));
  NCtoTF nctotf_65 (.A(equals_61_res), .res(nctotf_65_res));
  assign controlled_buffer_3_out = nctotf_65_res ? register_15_q : 8'bz;  // Controlled_Buffer controlled_buffer_31
  Equals equals_62 (.A(buscontrol_1_out_6), .B(increment_14_out_2), .res(equals_62_res));
  NCtoTF nctotf_66 (.A(equals_62_res), .res(nctotf_66_res));
  assign controlled_buffer_4_out = nctotf_66_res ? register_15_q : 8'bz;  // Controlled_Buffer controlled_buffer_32
  Equals equals_63 (.A(buscontrol_1_out_8), .B(increment_15_out_2), .res(equals_63_res));
  NCtoTF nctotf_67 (.A(equals_63_res), .res(nctotf_67_res));
  assign controlled_buffer_3_out = nctotf_67_res ? register_16_q : 8'bz;  // Controlled_Buffer controlled_buffer_33
  Equals equals_64 (.A(buscontrol_1_out_6), .B(increment_15_out_2), .res(equals_64_res));
  NCtoTF nctotf_68 (.A(equals_64_res), .res(nctotf_68_res));
  assign controlled_buffer_4_out = nctotf_68_res ? register_16_q : 8'bz;  // Controlled_Buffer controlled_buffer_34
  Equals equals_65 (.A(buscontrol_1_out_8), .B(increment_16_out_2), .res(equals_65_res));
  NCtoTF nctotf_69 (.A(equals_65_res), .res(nctotf_69_res));
  assign controlled_buffer_3_out = nctotf_69_res ? register_17_q : 8'bz;  // Controlled_Buffer controlled_buffer_35
  Equals equals_66 (.A(buscontrol_1_out_6), .B(increment_16_out_2), .res(equals_66_res));
  NCtoTF nctotf_70 (.A(equals_66_res), .res(nctotf_70_res));
  assign controlled_buffer_4_out = nctotf_70_res ? register_17_q : 8'bz;  // Controlled_Buffer controlled_buffer_36
  Equals equals_67 (.A(buscontrol_1_out_8), .B(increment_17_out_2), .res(equals_67_res));
  NCtoTF nctotf_71 (.A(equals_67_res), .res(nctotf_71_res));
  assign controlled_buffer_3_out = nctotf_71_res ? register_18_q : 8'bz;  // Controlled_Buffer controlled_buffer_37
  Equals equals_68 (.A(buscontrol_1_out_6), .B(increment_17_out_2), .res(equals_68_res));
  NCtoTF nctotf_72 (.A(equals_68_res), .res(nctotf_72_res));
  assign controlled_buffer_4_out = nctotf_72_res ? register_18_q : 8'bz;  // Controlled_Buffer controlled_buffer_38
  Equals equals_69 (.A(buscontrol_1_out_8), .B(increment_18_out_2), .res(equals_69_res));
  NCtoTF nctotf_73 (.A(equals_69_res), .res(nctotf_73_res));
  assign controlled_buffer_3_out = nctotf_73_res ? register_19_q : 8'bz;  // Controlled_Buffer controlled_buffer_39
  Equals equals_70 (.A(buscontrol_1_out_6), .B(increment_18_out_2), .res(equals_70_res));
  NCtoTF nctotf_74 (.A(equals_70_res), .res(nctotf_74_res));
  assign controlled_buffer_4_out = nctotf_74_res ? register_19_q : 8'bz;  // Controlled_Buffer controlled_buffer_40
  Equals equals_71 (.A(buscontrol_1_out_8), .B(increment_19_out_2), .res(equals_71_res));
  NCtoTF nctotf_75 (.A(equals_71_res), .res(nctotf_75_res));
  assign controlled_buffer_3_out = nctotf_75_res ? register_20_q : 8'bz;  // Controlled_Buffer controlled_buffer_41
  Equals equals_72 (.A(buscontrol_1_out_6), .B(increment_19_out_2), .res(equals_72_res));
  NCtoTF nctotf_76 (.A(equals_72_res), .res(nctotf_76_res));
  assign controlled_buffer_4_out = nctotf_76_res ? register_20_q : 8'bz;  // Controlled_Buffer controlled_buffer_42
  Equals equals_73 (.A(buscontrol_1_out_8), .B(increment_20_out_2), .res(equals_73_res));
  NCtoTF nctotf_77 (.A(equals_73_res), .res(nctotf_77_res));
  assign controlled_buffer_3_out = nctotf_77_res ? register_21_q : 8'bz;  // Controlled_Buffer controlled_buffer_43
  Equals equals_74 (.A(buscontrol_1_out_6), .B(increment_20_out_2), .res(equals_74_res));
  NCtoTF nctotf_78 (.A(equals_74_res), .res(nctotf_78_res));
  assign controlled_buffer_4_out = nctotf_78_res ? register_21_q : 8'bz;  // Controlled_Buffer controlled_buffer_44
  Equals equals_75 (.A(buscontrol_1_out_8), .B(increment_21_out_2), .res(equals_75_res));
  NCtoTF nctotf_79 (.A(equals_75_res), .res(nctotf_79_res));
  assign controlled_buffer_3_out = nctotf_79_res ? register_22_q : 8'bz;  // Controlled_Buffer controlled_buffer_45
  Equals equals_76 (.A(buscontrol_1_out_6), .B(increment_21_out_2), .res(equals_76_res));
  NCtoTF nctotf_80 (.A(equals_76_res), .res(nctotf_80_res));
  assign controlled_buffer_4_out = nctotf_80_res ? register_22_q : 8'bz;  // Controlled_Buffer controlled_buffer_46
  Equals equals_77 (.A(buscontrol_1_out_8), .B(increment_22_out_2), .res(equals_77_res));
  NCtoTF nctotf_81 (.A(equals_77_res), .res(nctotf_81_res));
  assign controlled_buffer_3_out = nctotf_81_res ? register_23_q : 8'bz;  // Controlled_Buffer controlled_buffer_47
  Equals equals_78 (.A(buscontrol_1_out_6), .B(increment_22_out_2), .res(equals_78_res));
  NCtoTF nctotf_82 (.A(equals_78_res), .res(nctotf_82_res));
  assign controlled_buffer_4_out = nctotf_82_res ? register_23_q : 8'bz;  // Controlled_Buffer controlled_buffer_48
  Equals equals_79 (.A(buscontrol_1_out_8), .B(increment_23_out_2), .res(equals_79_res));
  NCtoTF nctotf_83 (.A(equals_79_res), .res(nctotf_83_res));
  assign controlled_buffer_3_out = nctotf_83_res ? register_24_q : 8'bz;  // Controlled_Buffer controlled_buffer_49
  Equals equals_80 (.A(buscontrol_1_out_6), .B(increment_23_out_2), .res(equals_80_res));
  NCtoTF nctotf_84 (.A(equals_80_res), .res(nctotf_84_res));
  assign controlled_buffer_4_out = nctotf_84_res ? register_24_q : 8'bz;  // Controlled_Buffer controlled_buffer_50
  Equals equals_81 (.A(buscontrol_1_out_8), .B(increment_24_out_2), .res(equals_81_res));
  NCtoTF nctotf_85 (.A(equals_81_res), .res(nctotf_85_res));
  assign controlled_buffer_3_out = nctotf_85_res ? register_25_q : 8'bz;  // Controlled_Buffer controlled_buffer_51
  Equals equals_82 (.A(buscontrol_1_out_6), .B(increment_24_out_2), .res(equals_82_res));
  NCtoTF nctotf_86 (.A(equals_82_res), .res(nctotf_86_res));
  assign controlled_buffer_4_out = nctotf_86_res ? register_25_q : 8'bz;  // Controlled_Buffer controlled_buffer_52
  Equals equals_83 (.A(buscontrol_1_out_8), .B(increment_25_out_2), .res(equals_83_res));
  NCtoTF nctotf_87 (.A(equals_83_res), .res(nctotf_87_res));
  assign controlled_buffer_3_out = nctotf_87_res ? register_26_q : 8'bz;  // Controlled_Buffer controlled_buffer_53
  Equals equals_84 (.A(buscontrol_1_out_6), .B(increment_25_out_2), .res(equals_84_res));
  NCtoTF nctotf_88 (.A(equals_84_res), .res(nctotf_88_res));
  assign controlled_buffer_4_out = nctotf_88_res ? register_26_q : 8'bz;  // Controlled_Buffer controlled_buffer_54
  Equals equals_85 (.A(buscontrol_1_out_8), .B(increment_26_out_2), .res(equals_85_res));
  NCtoTF nctotf_89 (.A(equals_85_res), .res(nctotf_89_res));
  assign controlled_buffer_3_out = nctotf_89_res ? register_27_q : 8'bz;  // Controlled_Buffer controlled_buffer_55
  Equals equals_86 (.A(buscontrol_1_out_6), .B(increment_26_out_2), .res(equals_86_res));
  NCtoTF nctotf_90 (.A(equals_86_res), .res(nctotf_90_res));
  assign controlled_buffer_4_out = nctotf_90_res ? register_27_q : 8'bz;  // Controlled_Buffer controlled_buffer_56
  Equals equals_87 (.A(buscontrol_1_out_8), .B(increment_27_out_2), .res(equals_87_res));
  NCtoTF nctotf_91 (.A(equals_87_res), .res(nctotf_91_res));
  assign controlled_buffer_3_out = nctotf_91_res ? register_28_q : 8'bz;  // Controlled_Buffer controlled_buffer_57
  Equals equals_88 (.A(buscontrol_1_out_6), .B(increment_27_out_2), .res(equals_88_res));
  NCtoTF nctotf_92 (.A(equals_88_res), .res(nctotf_92_res));
  assign controlled_buffer_4_out = nctotf_92_res ? register_28_q : 8'bz;  // Controlled_Buffer controlled_buffer_58
  Equals equals_89 (.A(buscontrol_1_out_8), .B(increment_28_out_2), .res(equals_89_res));
  NCtoTF nctotf_93 (.A(equals_89_res), .res(nctotf_93_res));
  assign controlled_buffer_3_out = nctotf_93_res ? register_29_q : 8'bz;  // Controlled_Buffer controlled_buffer_59
  Equals equals_90 (.A(buscontrol_1_out_6), .B(increment_28_out_2), .res(equals_90_res));
  NCtoTF nctotf_94 (.A(equals_90_res), .res(nctotf_94_res));
  assign controlled_buffer_4_out = nctotf_94_res ? register_29_q : 8'bz;  // Controlled_Buffer controlled_buffer_60
  Equals equals_91 (.A(buscontrol_1_out_8), .B(increment_29_out_2), .res(equals_91_res));
  NCtoTF nctotf_95 (.A(equals_91_res), .res(nctotf_95_res));
  assign controlled_buffer_3_out = nctotf_95_res ? register_30_q : 8'bz;  // Controlled_Buffer controlled_buffer_61
  Equals equals_92 (.A(buscontrol_1_out_6), .B(increment_29_out_2), .res(equals_92_res));
  NCtoTF nctotf_96 (.A(equals_92_res), .res(nctotf_96_res));
  assign controlled_buffer_4_out = nctotf_96_res ? register_30_q : 8'bz;  // Controlled_Buffer controlled_buffer_62
  Equals equals_93 (.A(buscontrol_1_out_8), .B(increment_30_out_2), .res(equals_93_res));
  NCtoTF nctotf_97 (.A(equals_93_res), .res(nctotf_97_res));
  assign controlled_buffer_3_out = nctotf_97_res ? register_31_q : 8'bz;  // Controlled_Buffer controlled_buffer_63
  Equals equals_94 (.A(buscontrol_1_out_6), .B(increment_30_out_2), .res(equals_94_res));
  NCtoTF nctotf_98 (.A(equals_94_res), .res(nctotf_98_res));
  assign controlled_buffer_4_out = nctotf_98_res ? register_31_q : 8'bz;  // Controlled_Buffer controlled_buffer_64
  Equals equals_95 (.A(buscontrol_1_out_8), .B(increment_31_out_2), .res(equals_95_res));
  NCtoTF nctotf_99 (.A(equals_95_res), .res(nctotf_99_res));
  assign controlled_buffer_3_out = nctotf_99_res ? register_32_q : 8'bz;  // Controlled_Buffer controlled_buffer_65
  Equals equals_96 (.A(buscontrol_1_out_6), .B(increment_31_out_2), .res(equals_96_res));
  NCtoTF nctotf_100 (.A(equals_96_res), .res(nctotf_100_res));
  assign controlled_buffer_4_out = nctotf_100_res ? register_32_q : 8'bz;  // Controlled_Buffer controlled_buffer_66
  // Probe on Main_Programm_p3
  // Probe on Main_Programm_p4
  busControl buscontrol_1 (
    .in_1(buscontrol_3_out_8), .in_3(buscontrol_3_out_7), .in_5(Prepare_Register_q),
    .out_6(buscontrol_1_out_6), .out_8(buscontrol_1_out_8));  // open: in_2, in_4, out_7, out_9
  busControl buscontrol_2 (
    .in_2(controlled_buffer_74_out), .in_3(controlled_buffer_73_out), .in_5(Prepare_Register_q),
    .out_7(buscontrol_2_out_7), .out_8(buscontrol_2_out_8));  // open: in_1, in_4, out_6, out_9
  // Probe on Main_Programm_p5
  // Probe on Main_Programm_p6
  busControl buscontrol_3 (
    .in_1(Main_Programm_p3), .in_2(Main_Programm_p4), .in_3(Main_Programm_p5), .in_4(Main_Programm_p6),
    .in_5(Prepare_Register_q), .out_6(buscontrol_3_out_6), .out_7(buscontrol_3_out_7),
    .out_8(buscontrol_3_out_8), .out_9(buscontrol_3_out_9));
  Equals equals_97 (.A(buscontrol_3_out_6), .B(8'h1), .res(equals_97_res));
  Equals equals_98 (.A(buscontrol_3_out_6), .B(8'h2), .res(equals_98_res));
  Equals equals_99 (.A(buscontrol_3_out_6), .B(8'h3), .res(equals_99_res));
  Multiplexer #(.width(8)) multiplexer_1 (
    .in0(controlled_buffer_4_out), .in1(buscontrol_3_out_8), .out(multiplexer_1_out), .sel(equals_99_res));
  or or_5 (or_5_out, equals_97_res, equals_98_res, equals_99_res);
  SumMod summod_1 (
    .A(controlled_buffer_3_out), .B(multiplexer_1_out), .CarryIN(controlled_buffer_67_out),
    .CarryOUT(summod_1_carryout), .sign(summod_1_sign), .HalfCarryOUT(summod_1_halfcarryout),
    .isaZero(summod_1_isazero), .Result(summod_1_result), .NEV(summod_1_nev));
  assign controlled_buffer_67_out = equals_97_res ? register_33_q : 1'bz;  // Controlled_Buffer controlled_buffer_67
  assign controlled_buffer_68_out = or_5_out ? summod_1_halfcarryout : 1'bz;  // Controlled_Buffer controlled_buffer_68
  Register #(.width(1)) register_33 (
    .D(controlled_buffer_71_out), .en(tftonc_1_out_2), .clk(or_3_out), .Q(register_33_q),
    .clr(smallor_1_out_3));
  assign controlled_buffer_69_out = or_5_out ? summod_1_nev : 1'bz;  // Controlled_Buffer controlled_buffer_69
  assign controlled_buffer_70_out = or_5_out ? summod_1_sign : 1'bz;  // Controlled_Buffer controlled_buffer_70
  assign controlled_buffer_71_out = or_5_out ? summod_1_carryout : 1'bz;  // Controlled_Buffer controlled_buffer_71
  Register #(.width(1)) register_34 (
    .D(controlled_buffer_72_out), .en(tftonc_2_out_2), .clk(or_3_out), .Q(register_34_q),
    .clr(smallor_2_out_3));
  smallOR smallor_1 (.in_1(undriven_4), .in_2(or_2_out), .out_3(smallor_1_out_3));
  assign controlled_buffer_72_out = or_5_out ? summod_1_isazero : 1'bz;  // Controlled_Buffer controlled_buffer_72
  smallOR smallor_2 (.in_1(undriven_5), .in_2(or_2_out), .out_3(smallor_2_out_3));
  LedBar ledbar_1 (
    .led0(register_33_q), .led1(register_34_q), .led2(register_35_q), .led3(register_36_q),
    .led4(register_37_q), .led5(register_38_q), .led6(register_39_q), .led7(register_40_q));
  Register #(.width(1)) register_35 (
    .D(controlled_buffer_69_out), .en(tftonc_3_out_2), .clk(or_3_out), .Q(register_35_q),
    .clr(smallor_3_out_3));
  smallOR smallor_3 (.in_1(undriven_6), .in_2(or_2_out), .out_3(smallor_3_out_3));
  Register #(.width(1)) register_36 (
    .D(undriven_7), .en(tftonc_4_out_2), .clk(or_3_out), .Q(register_36_q), .clr(smallor_4_out_3));
  smallOR smallor_4 (.in_1(undriven_8), .in_2(or_2_out), .out_3(smallor_4_out_3));
  TFtoNC tftonc_1 (.in_1(or_5_out), .out_2(tftonc_1_out_2));
  TFtoNC tftonc_2 (.in_1(or_5_out), .out_2(tftonc_2_out_2));
  Register #(.width(1)) register_37 (
    .D(controlled_buffer_70_out), .en(tftonc_5_out_2), .clk(or_3_out), .Q(register_37_q),
    .clr(smallor_5_out_3));
  TFtoNC tftonc_3 (.in_1(or_5_out), .out_2(tftonc_3_out_2));
  Register #(.width(1)) register_38 (
    .D(controlled_buffer_68_out), .en(tftonc_6_out_2), .clk(or_3_out), .Q(register_38_q),
    .clr(smallor_6_out_3));
  smallOR smallor_5 (.in_1(undriven_9), .in_2(or_2_out), .out_3(smallor_5_out_3));
  TFtoNC tftonc_4 (.in_1(or_5_out), .out_2(tftonc_4_out_2));
  smallOR smallor_6 (.in_1(undriven_10), .in_2(or_2_out), .out_3(smallor_6_out_3));
  TFtoNC tftonc_5 (.in_1(or_5_out), .out_2(tftonc_5_out_2));
  TFtoNC tftonc_6 (.in_1(or_5_out), .out_2(tftonc_6_out_2));
  Register #(.width(1)) register_39 (
    .D(undriven_11), .en(undriven_12), .clk(or_3_out), .Q(register_39_q), .clr(smallor_7_out_3));
  smallOR smallor_7 (.in_1(undriven_13), .in_2(or_2_out), .out_3(smallor_7_out_3));
  Register #(.width(1)) register_40 (
    .D(undriven_14), .en(undriven_15), .clk(or_3_out), .Q(register_40_q), .clr(smallor_8_out_3));
  smallOR smallor_8 (.in_1(undriven_16), .in_2(or_2_out), .out_3(smallor_8_out_3));
  assign controlled_buffer_73_out = or_5_out ? summod_1_result : 8'bz;  // Controlled_Buffer controlled_buffer_73
  assign controlled_buffer_74_out = or_5_out ? buscontrol_3_out_9 : 8'bz;  // Controlled_Buffer controlled_buffer_74

  // Notes on the sheet:
  //   contents of Main_Programm (hex, n*v repeats v):
  //   3 1 f 1 3 2 1 2 1 1 2 3
  //   RED ADDR
  //   RES DATA
  //   MAIN DATA BUS
  //   OPCODE
  //   ADDR1
  //   SOBOL-0
  //   rev5
  //   ADDR2
  //   RESADDR
  //   RESET LINE
  //   MAIN PROGRAMM BUS
  //   C
  //   Z
  //   N
  //   SREG
  //   V
  //   S
  //   H
  //   T
  //   I
endmodule

// АЛП
module ALU (
  input  [7:0] opcode,
  input  [7:0] A,
  input  [7:0] B,
  output Carry,
  output [7:0] Result
);

  wire adder_1_cout, decoder_1_out0, decoder_1_out1, decoder_1_out2, decoder_1_out3, decoder_1_out4,
       decoder_1_out5, subtractor_1_bout;
  wire [7:0] adder_1_out, and_1_out, not_1_out, or_1_out, subtractor_1_out, xor_1_out;

  Decoder #(.enable("false"), .select(3)) decoder_1 (
    .out0(decoder_1_out0), .out1(decoder_1_out1), .out2(decoder_1_out2), .out3(decoder_1_out3),
    .out4(decoder_1_out4), .out5(decoder_1_out5), .sel(opcode[2:0]));  // open: out6, out7
  Adder adder_1 (.a(A), .b(B), .out(adder_1_out), .cout(adder_1_cout));  // open: cin
  Subtractor subtractor_1 (.a(A), .b(B), .out(subtractor_1_out), .bout(subtractor_1_bout));  // open: bin
  assign and_1_out = A & B;  // AND_Gate and_1, 8 bits wide
  assign or_1_out = A | B;  // OR_Gate or_1, 8 bits wide
  assign not_1_out = ~A;  // NOT_Gate not_1, 8 bits wide
  assign xor_1_out = A ^ B;  // XOR_Gate xor_1, 8 bits wide
  or or_2 (Carry, adder_1_cout, subtractor_1_bout);
  assign Result = decoder_1_out0 ? adder_1_out : 8'bz;  // Controlled_Buffer controlled_buffer_1
  assign Result = decoder_1_out1 ? subtractor_1_out : 8'bz;  // Controlled_Buffer controlled_buffer_2
  assign Result = decoder_1_out2 ? and_1_out : 8'bz;  // Controlled_Buffer controlled_buffer_3
  assign Result = decoder_1_out3 ? or_1_out : 8'bz;  // Controlled_Buffer controlled_buffer_4
  assign Result = decoder_1_out4 ? not_1_out : 8'bz;  // Controlled_Buffer controlled_buffer_5
  assign Result = decoder_1_out5 ? xor_1_out : 8'bz;  // Controlled_Buffer controlled_buffer_6
endmodule

// Срав.
module ComparatorMod (
  input  [7:0] L_d35cfc3e,
  input  [7:0] A,
  input  [7:0] B,
  output Result
);

  wire and_1_out, and_2_out, and_3_out, and_4_out, and_5_out, and_6_out, comparator_1_eq, comparator_1_gt,
       comparator_1_lt, comparator_2_eq, comparator_2_gt, comparator_2_lt, comparator_3_eq, comparator_3_gt,
       comparator_3_lt, comparator_4_eq, comparator_4_gt, comparator_4_lt, comparator_5_eq, comparator_5_gt,
       comparator_5_lt, comparator_6_eq, comparator_6_gt, comparator_6_lt, decoder_1_out0, decoder_1_out1,
       decoder_1_out2, decoder_1_out3, decoder_1_out4, decoder_1_out5, not_1_out, not_2_out, not_3_out,
       not_4_out, not_5_out, not_6_out, not_7_out, not_8_out, not_9_out, or_1_out, or_2_out, or_3_out;

  Decoder #(.enable("false"), .select(3)) decoder_1 (
    .out0(decoder_1_out0), .out1(decoder_1_out1), .out2(decoder_1_out2), .out3(decoder_1_out3),
    .out4(decoder_1_out4), .out5(decoder_1_out5), .sel(L_d35cfc3e[2:0]));  // open: out6, out7
  not not_1 (not_1_out, comparator_1_gt);
  Comparator comparator_1 (.a(A), .b(B), .gt(comparator_1_gt), .eq(comparator_1_eq), .lt(comparator_1_lt));
  not not_2 (not_2_out, comparator_1_lt);
  not not_3 (not_3_out, comparator_2_eq);
  Comparator comparator_2 (.a(A), .b(B), .gt(comparator_2_gt), .eq(comparator_2_eq), .lt(comparator_2_lt));
  not not_4 (not_4_out, comparator_3_gt);
  not not_5 (not_5_out, comparator_3_eq);
  Comparator comparator_3 (.a(A), .b(B), .gt(comparator_3_gt), .eq(comparator_3_eq), .lt(comparator_3_lt));
  not not_6 (not_6_out, comparator_4_gt);
  Comparator comparator_4 (.a(A), .b(B), .gt(comparator_4_gt), .eq(comparator_4_eq), .lt(comparator_4_lt));
  not not_7 (not_7_out, comparator_5_eq);
  Comparator comparator_5 (.a(A), .b(B), .gt(comparator_5_gt), .eq(comparator_5_eq), .lt(comparator_5_lt));
  not not_8 (not_8_out, comparator_5_lt);
  Comparator comparator_6 (.a(A), .b(B), .gt(comparator_6_gt), .eq(comparator_6_eq), .lt(comparator_6_lt));
  not not_9 (not_9_out, comparator_6_lt);
  and and_1 (and_1_out, not_1_out, comparator_1_eq, not_2_out);
  and and_2 (and_2_out, not_3_out, or_1_out);
  or or_1 (or_1_out, comparator_2_gt, comparator_2_lt);
  and and_3 (and_3_out, not_4_out, not_5_out, comparator_3_lt);
  and and_4 (and_4_out, not_6_out, or_2_out);
  or or_2 (or_2_out, comparator_4_eq, comparator_4_lt);
  and and_5 (and_5_out, comparator_5_gt, not_7_out, not_8_out);
  or or_3 (or_3_out, comparator_6_gt, comparator_6_eq);
  and and_6 (and_6_out, or_3_out, not_9_out);
  assign Result = decoder_1_out0 ? and_1_out : 1'bz;  // Controlled_Buffer controlled_buffer_1
  assign Result = decoder_1_out1 ? and_2_out : 1'bz;  // Controlled_Buffer controlled_buffer_2
  assign Result = decoder_1_out2 ? and_3_out : 1'bz;  // Controlled_Buffer controlled_buffer_3
  assign Result = decoder_1_out3 ? and_4_out : 1'bz;  // Controlled_Buffer controlled_buffer_4
  assign Result = decoder_1_out4 ? and_5_out : 1'bz;  // Controlled_Buffer controlled_buffer_5
  assign Result = decoder_1_out5 ? and_6_out : 1'bz;  // Controlled_Buffer controlled_buffer_6
endmodule

module RegisterMod (
  input  [7:0] Data,
  input  Save,
  input  Load,
  input  Clock,
  output [7:0] DataIfLoad,
  output [7:0] DataAlways
);

  wire and_1_out;

  Register Register8 (.D(Data), .en(1'b1), .clk(and_1_out), .Q(DataAlways));  // open: clr
  and and_1 (and_1_out, Save, Clock);
  assign DataIfLoad = Load ? DataAlways : 8'bz;  // Controlled_Buffer controlled_buffer_1
endmodule

module Equals (
  input  [7:0] A,
  input  [7:0] B,
  output res
);

  Comparator #(.mode("unsigned")) comparator_1 (.a(A), .b(B), .eq(res));  // open: gt, lt
endmodule

module eightbittoBCD (
  input  [7:0] in_1,
  output [3:0] firstdigit,
  output [3:0] seconddigit,
  output [3:0] thirddigit
);

  wire comparator_1_lt, comparator_2_gt;
  wire [7:0] divider_1_out, divider_1_rem, divider_2_out, divider_2_rem;

  Comparator #(.mode("unsigned")) comparator_1 (.a(8'h9), .b(in_1), .lt(comparator_1_lt));  // open: gt, eq
  Divider divider_1 (.a(in_1), .out(divider_1_out), .rem(divider_1_rem));  // open: b, upper
  Divider divider_2 (.a(divider_1_out), .b(8'ha), .out(divider_2_out), .rem(divider_2_rem));  // open: upper
  Comparator #(.mode("unsigned")) comparator_2 (.a(divider_1_out), .b(8'h9), .gt(comparator_2_gt));  // open: eq, lt
  Multiplexer #(.width(4)) multiplexer_1 (
    .in0(in_1[3:0]), .in1(divider_1_rem[3:0]), .out(firstdigit), .sel(comparator_1_lt));
  assign seconddigit = comparator_1_lt ? divider_2_out[3:0] : 4'bz;  // Controlled_Buffer controlled_buffer_1
  assign thirddigit = comparator_2_gt ? divider_2_rem[3:0] : 4'bz;  // Controlled_Buffer controlled_buffer_2
endmodule

module smallOR (
  input  in_1,
  input  in_2,
  output out_3
);

  or or_1 (out_3, in_1, in_2);
endmodule

module busControl (
  input  [7:0] in_1,
  input  [7:0] in_2,
  input  [7:0] in_3,
  input  [7:0] in_4,
  input  in_5,
  output [7:0] out_6,
  output [7:0] out_7,
  output [7:0] out_8,
  output [7:0] out_9
);

  assign out_9 = in_5 ? in_4 : 8'bz;  // Controlled_Buffer controlled_buffer_1
  assign out_6 = in_5 ? in_1 : 8'bz;  // Controlled_Buffer controlled_buffer_2
  assign out_7 = in_5 ? in_2 : 8'bz;  // Controlled_Buffer controlled_buffer_3
  assign out_8 = in_5 ? in_3 : 8'bz;  // Controlled_Buffer controlled_buffer_4
endmodule

module NCtoTF (
  input  A,
  output res
);


  assign res = A;
endmodule

module SumMod (
  input  CarryIN,
  input  [7:0] A,
  input  [7:0] B,
  output sign,
  output isaZero,
  output [7:0] Result,
  output CarryOUT,
  output HalfCarryOUT,
  output NEV
);

  Adder #(.width(3)) adder_1 (.a(A[2:0]), .b(B[2:0]), .out(Result[2:0]), .cin(CarryIN), .cout(HalfCarryOUT));
  Adder #(.width(4)) adder_2 (.a(A[6:3]), .b(B[6:3]), .out(Result[6:3]), .cin(HalfCarryOUT), .cout(NEV));
  Adder #(.width(1)) adder_3 (.a(A[7]), .b(B[7]), .out(Result[7]), .cin(NEV), .cout(CarryOUT));
  isZero iszero_1 (.in_1(Result), .out_2(isaZero));

  assign sign = Result[7];
endmodule

module bigControledBuffer (
  input  enable,
  input  A,
  output B_0,
  output B_1,
  output B_2,
  output B_3,
  output B_4,
  output B_5,
  output B_6,
  output B_7
);

  assign B_0 = enable ? A : 1'bz;  // Controlled_Buffer controlled_buffer_1
  assign B_1 = enable ? A : 1'bz;  // Controlled_Buffer controlled_buffer_2
  assign B_2 = enable ? A : 1'bz;  // Controlled_Buffer controlled_buffer_3
  assign B_3 = enable ? A : 1'bz;  // Controlled_Buffer controlled_buffer_4
  assign B_4 = enable ? A : 1'bz;  // Controlled_Buffer controlled_buffer_5
  assign B_5 = enable ? A : 1'bz;  // Controlled_Buffer controlled_buffer_6
  assign B_6 = enable ? A : 1'bz;  // Controlled_Buffer controlled_buffer_7
  assign B_7 = enable ? A : 1'bz;  // Controlled_Buffer controlled_buffer_8
endmodule

module TFtoNC (
  input  in_1,
  output out_2
);

  assign out_2 = in_1 ? in_1 : 1'bz;  // Controlled_Buffer controlled_buffer_1
endmodule

module isZero (
  input  [7:0] in_1,
  output out_2
);

  wire or_1_out, or_2_out, or_3_out, or_4_out;

  or or_1 (or_1_out, in_1[0], in_1[1], in_1[2]);
  or or_2 (or_2_out, in_1[3], in_1[4], in_1[5]);
  or or_3 (or_3_out, in_1[6], in_1[7]);
  or or_4 (or_4_out, or_1_out, or_2_out, or_3_out);
  not not_1 (out_2, or_4_out);
endmodule

module increment (
  input  [7:0] in_1,
  output [7:0] out_2
);

  Adder adder_1 (.a(8'h1), .b(in_1), .out(out_2));  // open: cin, cout
endmodule
